# Fritzing sketch prueba1 (saved by Fritzing 1.0.4)
breadboards: 1

parts:
  Mod1 = Amica NodeMCU DEVKIT 1.0
  microSD_Transflash1 = SparkFun - microSD Transflash

nets:
  N1: Mod1.pin1, Mod1.pin_10, Mod1.pin_26
  N2: Mod1.pin2, Mod1.pin_9, Mod1.pin_25, Mod1.pin_29, microSD_Transflash1.GND
  N3: Mod1.pin_30, microSD_Transflash1.VCC
